# Fritzing sketch schema-robot (saved by Fritzing 0.9.3b)

parts:
  SparkFun_Ardumoto_(L298N) = Monster Moto Shield
  Lipo_11_1V = LIPO-2000mAh [package=lipo-2000]
  M1 = Hobby Gearmotor with 48:1 gearbox [part_number=ROB-13302]
  M2 = Hobby Gearmotor with 48:1 gearbox [part_number=ROB-13302]
  Arduino_nano_33_IoT = Arduino Nano 33 IOT
  Arduino_nano_33_IoT1 = Arduino Nano 33 IOT
  Composant1 = Thumb Joystick
  U1 = LIPO-110mAh [package=lipo-110]

nets:
  N1: SparkFun_Ardumoto_(L298N).OUTA1, M2.pin_2
  N2: SparkFun_Ardumoto_(L298N).OUTB1, M2.pin_1
  N3: SparkFun_Ardumoto_(L298N).OUTA2, M1.pin_2
  N4: SparkFun_Ardumoto_(L298N).OUTB2, M1.pin_1
  N5: SparkFun_Ardumoto_(L298N).VCC, Lipo_11_1V.+
  N6: SparkFun_Ardumoto_(L298N).GND, Lipo_11_1V.-
  N7: SparkFun_Ardumoto_(L298N).PWM2_-_D6, Arduino_nano_33_IoT.D3~
  N8: SparkFun_Ardumoto_(L298N).INA1_-_D7, Arduino_nano_33_IoT.D4
  N9: SparkFun_Ardumoto_(L298N).INB1_-_D8, Arduino_nano_33_IoT.D6~
  N10: SparkFun_Ardumoto_(L298N).INB2_-_D9, Arduino_nano_33_IoT.D7
  N11: SparkFun_Ardumoto_(L298N).D10, Arduino_nano_33_IoT.D8
  N12: SparkFun_Ardumoto_(L298N).D11, Arduino_nano_33_IoT.D9~
  N13: Arduino_nano_33_IoT1.VIN, U1.+
  N14: Arduino_nano_33_IoT1.GND, Arduino_nano_33_IoT1.D13~, U1.-
  N15: Arduino_nano_33_IoT1.A6, Composant1.VERT
  N16: Arduino_nano_33_IoT1.A5, Composant1.HORZ

custom parts:
  Arduino Nano 33 IOT: The Arduino Nano 33 IoT is the easiest and cheapest point of entry to enhance existing devices (and creating new ones) to be part of the IoT and designing pico-network applications. Whether you are looking at building a sensor network connected to your office or home router, or if you want to create a BLE device sending data to a cellphone, the Nano 33 IoT is your one-stop-solution for many of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
